// Logisim project P3_ext.circ as structural Verilog: 8 circuits, main circuit test
module test (
  output [31:0] out_1,
  output out_2,
  output [4:0] out_3,
  output [31:0] out_4,
  output out_5,
  output [4:0] out_6,
  output [31:0] out_7
);

  wire clock_1_out, comparator_1_eq, counter_1_carry;
  wire [7:0] counter_1_q;

  Clock clock_1 (.out(clock_1_out));
  Counter counter_1 (.Q(counter_1_q), .carry(counter_1_carry), .clk(clock_1_out));  // open: load, D, count, clr
  // Probe on counter_1_carry
  Comparator comparator_1 (.a(8'h4), .b(counter_1_q), .eq(comparator_1_eq));  // open: gt, lt
  // Probe on out_1
  main main_1 (
    .Reset(comparator_1_eq), .out_2(out_1), .out_3(out_2), .out_4(out_3), .out_5(out_4), .out_6(out_5),
    .out_7(out_6), .out_8(out_7));
endmodule

module main (
  input  Reset,
  output [31:0] out_2,
  output out_3,
  output [4:0] out_4,
  output [31:0] out_5,
  output out_6,
  output [4:0] out_7,
  output [31:0] out_8
);

  wire ALUSrc, lh, MemWrite, out0, RegA, RegWrite, Zero;
  wire [1:0] alu_1_result, ExtOp, Mem2Reg, nPC_Sel, RegDst;
  wire [2:0] ALUOp;
  wire [4:0] MemAddr, multiplexer_2_out, RegAddr;
  wire [24:0] alu_1_result_2;
  wire [31:0] dm_1_rd, ext, MemData, multiplexer_3_out, PC_4, rdata1, RegData;

  IFU ifu_1 (
    .Zero(Zero), .nPC_Sel(nPC_Sel), .Reset(Reset), .jal_ext(ext), .jr_rdata1(rdata1), .PC_4(PC_4),
    .Instr(out_2));
  // Probe on out_2
  // Probe on out_2[5:0]
  // Probe on out_2[31:26]
  Comparator #(.width(32)) comparator_1 (.a(out_2), .b({32{1'b0}}), .eq(out0));  // open: gt, lt
  Controller controller_1 (
    .OpCode(out_2[31:26]), .Funct(out_2[5:0]), .RegDst(RegDst), .ALUSrc(ALUSrc), .Mem2Reg(Mem2Reg),
    .RegWrite(RegWrite), .MemWrite(MemWrite), .nPC_Sel(nPC_Sel), .ExtOp(ExtOp), .ALUOp(ALUOp), .RegA(RegA),
    .lh(lh));
  Multiplexer #(.select(2), .width(5)) multiplexer_1 (
    .in0(out_2[20:16]), .in1(out_2[15:11]), .in2({5{1'b1}}), .out(RegAddr), .sel(RegDst));  // open: in3, en
  Multiplexer #(.width(5)) multiplexer_2 (
    .in0(out_2[25:21]), .in1({5{1'b1}}), .out(multiplexer_2_out), .sel(RegA));  // open: en
  GRF grf_1 (
    .WE(RegWrite), .A1(multiplexer_2_out), .A2(out_2[20:16]), .A3(RegAddr), .WD(RegData), .Reset(Reset),
    .RD1(rdata1), .RD2(MemData));
  EXT ext_1 (.imm(out_2[15:0]), .instr_index(out_2[25:0]), .PC_4(PC_4), .ExtOp(ExtOp), .out_5(ext));
  Multiplexer #(.width(32)) multiplexer_3 (
    .in0(MemData), .in1(ext), .out(multiplexer_3_out), .sel(ALUSrc));  // open: en
  ALU alu_1 (
    .A(rdata1), .B(multiplexer_3_out), .ALUOp(ALUOp), .Zero(Zero),
    .result({alu_1_result_2, MemAddr, alu_1_result}));
  Multiplexer #(.select(2), .width(32)) multiplexer_4 (
    .in0({alu_1_result_2, MemAddr, alu_1_result}), .in1(dm_1_rd), .in2(PC_4), .out(RegData), .sel(Mem2Reg));  // open: in3, en
  DM dm_1 (
    .\byte (alu_1_result[1]), .A(MemAddr), .WD(MemData), .MemWrite(MemWrite), .Reset(Reset), .lh(lh),
    .RD(dm_1_rd));
  // Probe on out_2
  Multiplexer multiplexer_5 (.in0(RegWrite), .in1(1'b0), .out(out_3), .sel(out0));  // open: en
  Multiplexer #(.width(5)) multiplexer_6 (.in0(RegAddr), .in1({5{1'b0}}), .out(out_4), .sel(out0));  // open: en
  Multiplexer #(.width(32)) multiplexer_7 (.in0(RegData), .in1({32{1'b0}}), .out(out_5), .sel(out0));  // open: en
  Multiplexer multiplexer_8 (.in0(MemWrite), .in1(1'b0), .out(out_6), .sel(out0));  // open: en
  Multiplexer #(.width(5)) multiplexer_9 (.in0(MemAddr), .in1({5{1'b0}}), .out(out_7), .sel(out0));  // open: en
  Multiplexer #(.width(32)) multiplexer_10 (.in0(MemData), .in1({32{1'b0}}), .out(out_8), .sel(out0));  // open: en
  // Probe on out_8
  // Probe on out_4
  // Probe on out_5

  // Other names for the same wires on the sheet: Funct[5:0] = out_2[5:0]; Imm16[15:0] = out_2[15:0];
  //   Instr[31:0] = out_2; OpCode[5:0] = out_2[31:26]; rd[4:0] = out_2[15:11]; rs[4:0] = out_2[25:21];
  //   rt[4:0] = out_2[20:16]
endmodule

module IFU (
  input  Zero,
  input  [1:0] nPC_Sel,
  input  Reset,
  input  [31:0] jal_ext,
  input  [31:0] jr_rdata1,
  output [31:0] PC_4,
  output [31:0] Instr
);

  wire clock_1_out;
  wire [31:0] beq, bit_extender_1_out, multiplexer_1_out, multiplexer_2_out, register_1_q;

  Multiplexer #(.width(32)) multiplexer_1 (.in0(PC_4), .in1(beq), .out(multiplexer_1_out), .sel(Zero));  // open: en
  Multiplexer #(.select(2), .width(32)) multiplexer_2 (
    .in0(PC_4), .in1(multiplexer_1_out), .in2(jal_ext), .in3(jr_rdata1), .out(multiplexer_2_out),
    .sel(nPC_Sel));  // open: en
  assign bit_extender_1_out = {{14{Instr[15]}}, {Instr[15:0], 2'b00}};  // Bit_Extender bit_extender_1
  Register #(.width(32)) register_1 (
    .D(multiplexer_2_out), .Q(register_1_q), .clk(clock_1_out), .clr(Reset));  // open: en
  Clock clock_1 (.out(clock_1_out));
  Adder #(.width(32)) adder_1 (.a(32'h4), .b(register_1_q), .out(PC_4));  // open: cin, cout
  Adder #(.width(32)) adder_2 (.a(PC_4), .b(bit_extender_1_out), .out(beq));  // open: cin, cout
  ROM #(.addrWidth(5), .dataWidth(32)) rom_1 (.addr(register_1_q[6:2]), .data(Instr));  // open: sel

  // Notes on the sheet:
  //   contents of rom_1 (hex, n*v repeats v):
  //   34080000 3405007b 3407ffff 3c0ef0ff ad070000 ad0e0004 ad050028 c000c09 8000c0c ad050024 0 3e00008
  //   850a0000 850a0006 388f0002 38af007b
endmodule

module GRF (
  input  Reset,
  input  WE,
  input  [4:0] A1,
  input  [4:0] A2,
  input  [4:0] A3,
  input  [31:0] WD,
  output [31:0] RD1,
  output [31:0] RD2
);

  wire clock_1_out, demultiplexer_1_out0, demultiplexer_1_out1, demultiplexer_1_out2, demultiplexer_1_out3,
       demultiplexer_1_out4, demultiplexer_1_out5, demultiplexer_1_out6, demultiplexer_1_out7,
       demultiplexer_1_out8, demultiplexer_1_out9, demultiplexer_1_out10, demultiplexer_1_out11,
       demultiplexer_1_out12, demultiplexer_1_out13, demultiplexer_1_out14, demultiplexer_1_out15,
       demultiplexer_1_out16, demultiplexer_1_out17, demultiplexer_1_out18, demultiplexer_1_out19,
       demultiplexer_1_out20, demultiplexer_1_out21, demultiplexer_1_out22, demultiplexer_1_out23,
       demultiplexer_1_out24, demultiplexer_1_out25, demultiplexer_1_out26, demultiplexer_1_out27,
       demultiplexer_1_out28, demultiplexer_1_out29, demultiplexer_1_out30, demultiplexer_1_out31;
  wire [31:0] _0, _1, _2, _3, _4, _5, _6, _7, _8, _9, _10, _11, _12, _13, _14, _15, _16, _17, _18, _19, _20,
       _21, _22, _23, _24, _25, _26, _27, _28, _29, _30, _31;

  Demultiplexer #(.select(5)) demultiplexer_1 (
    .out0(demultiplexer_1_out0), .out1(demultiplexer_1_out1), .out2(demultiplexer_1_out2),
    .out3(demultiplexer_1_out3), .out4(demultiplexer_1_out4), .out5(demultiplexer_1_out5),
    .out6(demultiplexer_1_out6), .out7(demultiplexer_1_out7), .out8(demultiplexer_1_out8),
    .out9(demultiplexer_1_out9), .out10(demultiplexer_1_out10), .out11(demultiplexer_1_out11),
    .out12(demultiplexer_1_out12), .out13(demultiplexer_1_out13), .out14(demultiplexer_1_out14),
    .out15(demultiplexer_1_out15), .out16(demultiplexer_1_out16), .out17(demultiplexer_1_out17),
    .out18(demultiplexer_1_out18), .out19(demultiplexer_1_out19), .out20(demultiplexer_1_out20),
    .out21(demultiplexer_1_out21), .out22(demultiplexer_1_out22), .out23(demultiplexer_1_out23),
    .out24(demultiplexer_1_out24), .out25(demultiplexer_1_out25), .out26(demultiplexer_1_out26),
    .out27(demultiplexer_1_out27), .out28(demultiplexer_1_out28), .out29(demultiplexer_1_out29),
    .out30(demultiplexer_1_out30), .out31(demultiplexer_1_out31), .in(WE), .sel(A3));  // open: en
  Clock clock_1 (.out(clock_1_out));
  Register #(.width(32)) register_1 (.en(demultiplexer_1_out0), .Q(_0), .clk(clock_1_out), .clr(Reset));  // open: D
  Register #(.width(32)) register_2 (.D(WD), .en(demultiplexer_1_out4), .Q(_4), .clk(clock_1_out), .clr(Reset));
  Register #(.width(32)) register_3 (.D(WD), .en(demultiplexer_1_out8), .Q(_8), .clk(clock_1_out), .clr(Reset));
  Register #(.width(32)) register_4 (.D(WD), .en(demultiplexer_1_out12), .Q(_12), .clk(clock_1_out), .clr(Reset));
  Register #(.width(32)) register_5 (.D(WD), .en(demultiplexer_1_out16), .Q(_16), .clk(clock_1_out), .clr(Reset));
  Register #(.width(32)) register_6 (.D(WD), .en(demultiplexer_1_out20), .Q(_20), .clk(clock_1_out), .clr(Reset));
  Register #(.width(32)) register_7 (.D(WD), .en(demultiplexer_1_out24), .Q(_24), .clk(clock_1_out), .clr(Reset));
  Register #(.width(32)) register_8 (.D(WD), .en(demultiplexer_1_out28), .Q(_28), .clk(clock_1_out), .clr(Reset));
  Register #(.width(32)) register_9 (.D(WD), .en(demultiplexer_1_out1), .Q(_1), .clk(clock_1_out), .clr(Reset));
  Register #(.width(32)) register_10 (.D(WD), .en(demultiplexer_1_out5), .Q(_5), .clk(clock_1_out), .clr(Reset));
  Register #(.width(32)) register_11 (.D(WD), .en(demultiplexer_1_out9), .Q(_9), .clk(clock_1_out), .clr(Reset));
  Register #(.width(32)) register_12 (.D(WD), .en(demultiplexer_1_out13), .Q(_13), .clk(clock_1_out), .clr(Reset));
  Register #(.width(32)) register_13 (.D(WD), .en(demultiplexer_1_out17), .Q(_17), .clk(clock_1_out), .clr(Reset));
  Register #(.width(32)) register_14 (.D(WD), .en(demultiplexer_1_out21), .Q(_21), .clk(clock_1_out), .clr(Reset));
  Register #(.width(32)) register_15 (.D(WD), .en(demultiplexer_1_out25), .Q(_25), .clk(clock_1_out), .clr(Reset));
  Register #(.width(32)) register_16 (.D(WD), .en(demultiplexer_1_out29), .Q(_29), .clk(clock_1_out), .clr(Reset));
  Register #(.width(32)) register_17 (.D(WD), .en(demultiplexer_1_out2), .Q(_2), .clk(clock_1_out), .clr(Reset));
  Register #(.width(32)) register_18 (.D(WD), .en(demultiplexer_1_out6), .Q(_6), .clk(clock_1_out), .clr(Reset));
  Register #(.width(32)) register_19 (.D(WD), .en(demultiplexer_1_out10), .Q(_10), .clk(clock_1_out), .clr(Reset));
  Register #(.width(32)) register_20 (.D(WD), .en(demultiplexer_1_out14), .Q(_14), .clk(clock_1_out), .clr(Reset));
  Register #(.width(32)) register_21 (.D(WD), .en(demultiplexer_1_out18), .Q(_18), .clk(clock_1_out), .clr(Reset));
  Register #(.width(32)) register_22 (.D(WD), .en(demultiplexer_1_out22), .Q(_22), .clk(clock_1_out), .clr(Reset));
  Register #(.width(32)) register_23 (.D(WD), .en(demultiplexer_1_out26), .Q(_26), .clk(clock_1_out), .clr(Reset));
  Register #(.width(32)) register_24 (.D(WD), .en(demultiplexer_1_out30), .Q(_30), .clk(clock_1_out), .clr(Reset));
  Register #(.width(32)) register_25 (.D(WD), .en(demultiplexer_1_out3), .Q(_3), .clk(clock_1_out), .clr(Reset));
  Register #(.width(32)) register_26 (.D(WD), .en(demultiplexer_1_out7), .Q(_7), .clk(clock_1_out), .clr(Reset));
  Register #(.width(32)) register_27 (.D(WD), .en(demultiplexer_1_out11), .Q(_11), .clk(clock_1_out), .clr(Reset));
  Register #(.width(32)) register_28 (.D(WD), .en(demultiplexer_1_out15), .Q(_15), .clk(clock_1_out), .clr(Reset));
  Register #(.width(32)) register_29 (.D(WD), .en(demultiplexer_1_out19), .Q(_19), .clk(clock_1_out), .clr(Reset));
  Register #(.width(32)) register_30 (.D(WD), .en(demultiplexer_1_out23), .Q(_23), .clk(clock_1_out), .clr(Reset));
  Register #(.width(32)) register_31 (.D(WD), .en(demultiplexer_1_out27), .Q(_27), .clk(clock_1_out), .clr(Reset));
  Register #(.width(32)) register_32 (.D(WD), .en(demultiplexer_1_out31), .Q(_31), .clk(clock_1_out), .clr(Reset));
  Multiplexer #(.select(5), .width(32)) multiplexer_1 (
    .in0(_0), .in1(_1), .in2(_2), .in3(_3), .in4(_4), .in5(_5), .in6(_6), .in7(_7), .in8(_8), .in9(_9),
    .in10(_10), .in11(_11), .in12(_12), .in13(_13), .in14(_14), .in15(_15), .in16(_16), .in17(_17),
    .in18(_18), .in19(_19), .in20(_20), .in21(_21), .in22(_22), .in23(_23), .in24(_24), .in25(_25),
    .in26(_26), .in27(_27), .in28(_28), .in29(_29), .in30(_30), .in31(_31), .out(RD1), .sel(A1));  // open: en
  Multiplexer #(.select(5), .width(32)) multiplexer_2 (
    .in0(_0), .in1(_1), .in2(_2), .in3(_3), .in4(_4), .in5(_5), .in6(_6), .in7(_7), .in8(_8), .in9(_9),
    .in10(_10), .in11(_11), .in12(_12), .in13(_13), .in14(_14), .in15(_15), .in16(_16), .in17(_17),
    .in18(_18), .in19(_19), .in20(_20), .in21(_21), .in22(_22), .in23(_23), .in24(_24), .in25(_25),
    .in26(_26), .in27(_27), .in28(_28), .in29(_29), .in30(_30), .in31(_31), .out(RD2), .sel(A2));  // open: en
endmodule

module ALU (
  input  [31:0] A,
  input  [31:0] B,
  input  [2:0] ALUOp,
  output Zero,
  output [31:0] result
);

  wire [31:0] adder_1_out, or_1_out, subtractor_1_out, xor_1_out;

  Adder #(.width(32)) adder_1 (.a(A), .b(B), .out(adder_1_out));  // open: cin, cout
  Subtractor #(.width(32)) subtractor_1 (.a(A), .b(B), .out(subtractor_1_out));  // open: bin, bout
  assign or_1_out = A | B;  // OR_Gate or_1, 32 bits wide
  assign xor_1_out = A ^ B;  // XOR_Gate xor_1, 32 bits wide
  Multiplexer #(.select(3), .width(32)) multiplexer_1 (
    .in0(adder_1_out), .in1(subtractor_1_out), .in2(or_1_out), .in3(B), .in4(xor_1_out), .out(result),
    .sel(ALUOp));  // open: in5, in6, in7, en
  Comparator #(.width(32), .mode("unsigned")) comparator_1 (.a({32{1'b0}}), .b(result), .eq(Zero));  // open: gt, lt
endmodule

module DM (
  input  \byte ,
  input  [4:0] A,
  input  [31:0] WD,
  input  lh,
  input  MemWrite,
  input  Reset,
  output [31:0] RD
);

  wire clock_1_out;
  wire [15:0] multiplexer_1_out;
  wire [31:0] bit_extender_1_out, ram_1_data;

  Clock clock_1 (.out(clock_1_out));
  RAM #(.addrWidth(5), .dataWidth(32), .bus("separate")) ram_1 (
    .addr(A), .din(WD), .data(ram_1_data), .str(MemWrite), .clk(clock_1_out), .clr(Reset));  // open: sel, ld
  Multiplexer #(.width(16)) multiplexer_1 (
    .in0(ram_1_data[15:0]), .in1(ram_1_data[31:16]), .out(multiplexer_1_out), .sel(\byte ));  // open: en
  assign bit_extender_1_out = {{16{multiplexer_1_out[15]}}, multiplexer_1_out};  // Bit_Extender bit_extender_1
  Multiplexer #(.width(32)) multiplexer_2 (.in0(ram_1_data), .in1(bit_extender_1_out), .out(RD), .sel(lh));  // open: en
endmodule

module EXT (
  input  [15:0] imm,
  input  [25:0] instr_index,
  input  [1:0] ExtOp,
  input  [31:0] PC_4,
  output [31:0] out_5
);

  wire [31:0] bit_extender_1_out, bit_extender_2_out, subtractor_1_out;

  Subtractor #(.width(32)) subtractor_1 (.a(PC_4), .b(32'h4), .out(subtractor_1_out));  // open: bin, bout
  assign bit_extender_1_out = {{16{imm[15]}}, imm};  // Bit_Extender bit_extender_1
  assign bit_extender_2_out = {{16{1'b0}}, imm};  // Bit_Extender bit_extender_2
  Multiplexer #(.select(2), .width(32)) multiplexer_1 (
    .in0(bit_extender_2_out), .in1({imm, {16{1'b0}}}), .in2({subtractor_1_out[31:28], instr_index, 2'b00}),
    .in3(bit_extender_1_out), .out(out_5), .sel(ExtOp));  // open: en
endmodule

module Controller (
  input  [5:0] OpCode,
  input  [5:0] Funct,
  output RegA,
  output [1:0] RegDst,
  output ALUSrc,
  output [1:0] Mem2Reg,
  output RegWrite,
  output MemWrite,
  output [1:0] nPC_Sel,
  output [1:0] ExtOp,
  output [2:0] ALUOp,
  output lh
);

  wire addu, beq, j, jal, lui, lw, ori, subu, sw, xori;

  and u_addu (addu, ~OpCode[5], ~OpCode[4], ~OpCode[3], ~OpCode[2], ~OpCode[1], ~OpCode[0], Funct[5], ~Funct[4], ~Funct[3], ~Funct[2], ~Funct[1], Funct[0]);  // AND_Gate
  and u_subu (subu, ~OpCode[5], ~OpCode[4], ~OpCode[3], ~OpCode[2], ~OpCode[1], ~OpCode[0], Funct[5], ~Funct[4], ~Funct[3], ~Funct[2], Funct[1], Funct[0]);  // AND_Gate
  and u_ori (ori, ~OpCode[5], ~OpCode[4], OpCode[3], OpCode[2], ~OpCode[1], OpCode[0]);  // AND_Gate
  and u_lw (lw, OpCode[5], ~OpCode[4], ~OpCode[3], ~OpCode[2], OpCode[1], OpCode[0]);  // AND_Gate
  and u_sw (sw, OpCode[5], ~OpCode[4], OpCode[3], ~OpCode[2], OpCode[1], OpCode[0]);  // AND_Gate
  and u_beq (beq, ~OpCode[5], ~OpCode[4], ~OpCode[3], OpCode[2], ~OpCode[1], ~OpCode[0]);  // AND_Gate
  and u_lui (lui, ~OpCode[5], ~OpCode[4], OpCode[3], OpCode[2], OpCode[1], OpCode[0]);  // AND_Gate
  and u_jal (jal, ~OpCode[5], ~OpCode[4], ~OpCode[3], ~OpCode[2], OpCode[1], OpCode[0]);  // AND_Gate
  and jr (RegA, ~OpCode[5], ~OpCode[4], ~OpCode[3], ~OpCode[2], ~OpCode[1], ~OpCode[0], ~Funct[5], ~Funct[4], Funct[3], ~Funct[2], ~Funct[1], ~Funct[0]);  // AND_Gate
  and u_j (j, ~OpCode[5], ~OpCode[4], ~OpCode[3], ~OpCode[2], OpCode[1], ~OpCode[0]);  // AND_Gate
  and u_xori (xori, ~OpCode[5], ~OpCode[4], OpCode[3], OpCode[2], OpCode[1], ~OpCode[0]);  // AND_Gate
  and u_lh (lh, OpCode[5], ~OpCode[4], ~OpCode[3], ~OpCode[2], ~OpCode[1], OpCode[0]);  // AND_Gate
  or RegDst_1 (RegDst[1], jal, 1'b0);
  or RegDst_0 (RegDst[0], addu, subu);
  or u_ALUSrc (ALUSrc, ori, lw, sw, lui, xori, lh);
  or Mem2Reg_1 (Mem2Reg[1], jal, 1'b0);
  or Mem2Reg_0 (Mem2Reg[0], lw, lh);
  or u_RegWrite (RegWrite, addu, subu, ori, lw, lui, jal, xori, lh);
  or u_MemWrite (MemWrite, sw, 1'b0);
  or nPC_Sel_1 (nPC_Sel[1], jal, RegA, j);
  or nPC_Sel_0 (nPC_Sel[0], beq, RegA);
  or ExtOp_1 (ExtOp[1], sw, jal, j, lh);
  or ExtOp_0 (ExtOp[0], sw, lui, lh);
  or ALUOp_2 (ALUOp[2], xori, 1'b0);
  or ALUOp_1 (ALUOp[1], ori, lui);
  or ALUOp_0 (ALUOp[0], subu, beq, lui);

  // Other names for the same wires on the sheet: jr = RegA; Op[5:0] = OpCode
endmodule
